# Fritzing sketch L293D Motor Driver Circuit Diagram (saved by Fritzing 0.7.11b)
breadboards: 1

parts:
  IC1 = L293D [package=THT]
  M1 = DC Motor
  M2 = DC Motor
  J1 = Screw terminal - 2 pins [package=THT]
  J2 = Screw terminal - 2 pins [package=THT]
  DC_Power1 = DC Power [voltage=5]

nets:
  N1: IC1.Enable_1, IC1.Enable_2, IC1.+V
  N2: IC1.In_1, J2.pin2
  N3: IC1.Out_1_(_Controlled_by_Enable_1_), M2.pin_2
  GND: IC1.0V, DC_Power1.GND
  N4: IC1.Out_2_(_Controlled_by_Enable_1_), M2.pin_1
  N5: IC1.In_2, J2.pin1
  N6: IC1.+Vmotor, DC_Power1.V+
  N7: IC1.In_3, J1.pin2
  N8: IC1.Out_3_(_Controlled_by_Enable_2_), M1.pin_2
  N9: IC1.Out_4_(_Controlled_by_Enable_2_), M1.pin_1
  N10: IC1.In_4, J1.pin1

notes:
  To Arduino Pin :
  Pin 2 -------->
  Pin 3 -------->
  To Arduino Pin :
  <---------- Pin 4
  <---------- Pin 5
